# Fritzing sketch schema (saved by Fritzing 0.9.3b)
circuit board: 8.46667cm x 5.64444cm
breadboards: 1

parts:
  Composant1 = Arduino Uno (Rev3)
  J1 = Piezo Speaker
  R1 = Resistor [tolerance=±1% resistance=100k package=THT]
  R2 = Resistor [tolerance=±1% resistance=100k package=THT]
  R3 = Resistor [tolerance=±1% resistance=220k package=THT]
  LCD1 = LCD screen
  LCM1602_IIC2 = LCM1602 IIC [part_number="LCM1602 IIC" chip_label="LCM1602 IIC" package="DIP (Dual Inline) [THT]"]
  R4 = Resistor [tolerance=±1% resistance=470k package=THT]
  R5 = Resistor [tolerance=±1% resistance=510k package=THT]
  R6 = Resistor [tolerance=±1% resistance=1M package=THT]
  switch1 = Rotary_Switch_12x1

nets:
  N1: Composant1.A0, J1.pin2, R3.Pin_1, R4.Pin_1, R5.Pin_1, R6.Pin_1, switch1.0
  N2: Composant1.A4/SDA, LCM1602_IIC2.SDA
  N3: Composant1.A5/SCL, LCM1602_IIC2.SCL
  5V: Composant1.5V, R1.Pin_0, LCM1602_IIC2.VCC
  GND: Composant1.GND, R2.Pin_1, LCM1602_IIC2.GND
  N4: J1.pin1, R1.Pin_1, R2.Pin_0, R3.Pin_0, R4.Pin_0, R5.Pin_0, R6.Pin_0
  VSS: LCD1.VSS, LCM1602_IIC2.VSS
  VDD: LCD1.VDD, LCM1602_IIC2.VDD
  N5: LCD1.V0, LCM1602_IIC2.V0
  N6: LCD1.RS, LCM1602_IIC2.RS
  N7: LCD1.R/W, LCM1602_IIC2.RW
  N8: LCD1.E, LCM1602_IIC2.E
  N9: LCD1.DB0, LCM1602_IIC2.D0
  N10: LCD1.DB1, LCM1602_IIC2.D1
  N11: LCD1.DB2, LCM1602_IIC2.D2
  N12: LCD1.DB3, LCM1602_IIC2.D3
  N13: LCD1.DB4, LCM1602_IIC2.D4
  N14: LCD1.DB5, LCM1602_IIC2.D5
  N15: LCD1.DB6, LCM1602_IIC2.D6
  N16: LCD1.DB7, LCM1602_IIC2.D7
  N17: LCD1.LED+, LCM1602_IIC2.A
  N18: LCD1.LED-, LCM1602_IIC2.K
  N19: switch1.9, switch1.10, switch1.11, switch1.12

custom parts:
  LCM1602 IIC: I2C-Module to use a 1602 or 2004 LCD on with the wire.h libory Serial LCD Modul
